// Logisim project Calc_Logic.circ as structural Verilog: 11 circuits, main circuit main
module main (
  input  s2,
  input  s1,
  input  s0,
  input  pwr,
  input  clr,
  input  num,
  input  op,
  input  neg
);

  wire add_out, b0_out, b1_out, b2_out, b3_out, b4_out, b5_out, b6_out, b7_out, b8_out, b9_out, clock_1_out,
       controller_1_clrs, controller_1_enables, controller_1_n_or_i, controller_1_val1_en, div_out, mult_out,
       sub_out;
  wire [2:0] controller_1_n0, register_1_q;
  wire [3:0] num_encoder_1_out_11;

  Button b1 (.out(b1_out));
  Button b4 (.out(b4_out));
  Button b7 (.out(b7_out));
  Button add (.out(add_out));
  Button sub (.out(sub_out));
  Button div (.out(div_out));
  Button mult (.out(mult_out));
  Button b2 (.out(b2_out));
  Button b5 (.out(b5_out));
  Button b8 (.out(b8_out));
  Button b0 (.out(b0_out));
  Button b3 (.out(b3_out));
  Button b6 (.out(b6_out));
  Button b9 (.out(b9_out));
  op_encoder op_encoder_1 (.add(add_out), .sub(sub_out), .div(div_out), .mult(mult_out));  // open: out_5
  controller controller_1 (
    .s2(register_1_q[2]), .s1(register_1_q[1]), .s0(register_1_q[0]), .pwr(pwr), .clr(clr), .num(num),
    .op(op), .neg(neg), .n_or_i(controller_1_n_or_i), .enables(controller_1_enables),
    .clrs(controller_1_clrs), .val1_en(controller_1_val1_en), .n2(controller_1_n0[2]),
    .n1(controller_1_n0[1]), .n0(controller_1_n0[0]));
  num_encoder num_encoder_1 (
    .n0(b0_out), .n1(b1_out), .n2(b2_out), .n3(b3_out), .n4(b4_out), .n5(b5_out), .n6(b6_out), .n7(b7_out),
    .n8(b8_out), .n9(b9_out), .out_11(num_encoder_1_out_11));
  Clock clock_1 (.out(clock_1_out));
  Register #(.width(3)) register_1 (.D(controller_1_n0), .en(1'b1), .clk(clock_1_out), .Q(register_1_q));  // open: clr
endmodule

module controller (
  input  s2,
  input  s1,
  input  s0,
  input  pwr,
  input  clr,
  input  num,
  input  op,
  input  neg,
  output n_or_i,
  output enables,
  output clrs,
  output val1_en,
  output n2,
  output n1,
  output n0
);

  wire not_1_out, not_2_out, not_3_out, not_4_out, not_5_out, not_6_out, not_7_out, not_8_out, xor_1_out;

  not not_1 (not_1_out, s2);
  not not_2 (not_2_out, s1);
  not not_3 (not_3_out, s0);
  not not_4 (not_4_out, pwr);
  not not_5 (not_5_out, clr);
  not not_6 (not_6_out, num);
  not not_7 (not_7_out, op);
  and and_1 (clrs, not_2_out, not_1_out);
  and and_2 (enables, not_3_out, not_2_out);
  xor xor_1 (xor_1_out, s1, s2);
  and and_3 (val1_en, s0, xor_1_out);
  n2_logic n2_logic_1 (
    .s2_not(not_1_out), .s1(s1), .s0_not(not_3_out), .pwr_not(not_4_out), .clr_not(not_5_out),
    .num_not(not_6_out), .op(op), .neg(neg), .n2_out(n2));
  not not_8 (not_8_out, neg);
  n1_logic n1_logic_1 (
    .s2(s2), .s1(s1), .s0(s0), .pwr_n(not_4_out), .clr_n(not_5_out), .num(num), .op_n(not_7_out),
    .neg_n(not_8_out), .n1_output(n1));
  n0_logic n0_logic_1 (
    .s2(s2), .s1(s1), .s0(s0), .pwr(pwr), .clr(clr), .num(num), .op_n(not_7_out), .neg(neg), .n0_clr(n0));

  assign n_or_i = s1;

  // Notes on the sheet:
  //   op_clr
  //   val1_clr
  //   val2_clr
  //   regs_clr
  //   val2_en
  //   eval_en
  //   opcode_en
endmodule

module n2_logic (
  input  s2_not,
  input  s1,
  input  s0_not,
  input  pwr_not,
  input  clr_not,
  input  num_not,
  input  op,
  input  neg,
  output n2_out
);

  wire and_1_out, and_2_out, and_3_out, and_4_out, and_5_out, and_6_out, not_1_out, or_1_out;

  and and_1 (and_1_out, s2_not, s1);
  not not_1 (not_1_out, op);
  and and_2 (and_2_out, and_1_out, s0_not);
  and and_3 (and_3_out, and_2_out, pwr_not);
  and and_4 (and_4_out, and_3_out, clr_not);
  and and_5 (and_5_out, not_1_out, neg);
  and and_6 (and_6_out, and_4_out, num_not);
  or or_1 (or_1_out, op, and_5_out);
  and and_7 (n2_out, and_6_out, or_1_out);
endmodule

module n1_logic (
  input  s2,
  input  s1,
  input  s0,
  input  pwr_n,
  input  clr_n,
  input  num,
  input  op_n,
  input  neg_n,
  output n1_output
);

  wire and_1_out, and_2_out, and_3_out, and_4_out, and_5_out, and_6_out, and_7_out, not_1_out, not_2_out,
       not_3_out, not_4_out, or_1_out, or_2_out, or_3_out;

  not not_1 (not_1_out, s2);
  not not_2 (not_2_out, s0);
  not not_3 (not_3_out, num);
  and and_1 (and_1_out, not_3_out, op_n);
  or or_1 (or_1_out, num, and_2_out);
  and and_2 (and_2_out, and_1_out, neg_n);
  and and_3 (and_3_out, not_2_out, or_1_out);
  not not_4 (not_4_out, s1);
  and and_4 (and_4_out, s1, and_3_out);
  or or_2 (or_2_out, s0, and_4_out);
  and and_5 (and_5_out, s2, not_4_out);
  and and_6 (and_6_out, not_1_out, or_2_out);
  and and_7 (and_7_out, pwr_n, clr_n);
  or or_3 (or_3_out, and_5_out, and_6_out);
  and and_8 (n1_output, and_7_out, or_3_out);
endmodule

module n0_logic (
  input  s2,
  input  s1,
  input  s0,
  input  pwr,
  input  clr,
  input  num,
  input  op_n,
  input  neg,
  output n0_clr
);

  wire and_1_out, and_2_out, and_3_out, and_4_out, and_5_out, and_6_out, and_7_out, and_8_out, and_9_out,
       and_10_out, and_11_out, and_12_out, and_13_out, not_1_out, not_2_out, not_3_out, not_4_out, not_5_out,
       not_6_out, or_1_out, or_2_out, or_3_out, or_4_out;

  not not_1 (not_1_out, s2);
  not not_2 (not_2_out, s1);
  not not_3 (not_3_out, s0);
  not not_4 (not_4_out, pwr);
  not not_5 (not_5_out, clr);
  not not_6 (not_6_out, num);
  and and_1 (and_1_out, not_6_out, op_n);
  or or_1 (or_1_out, num, and_2_out);
  and and_2 (and_2_out, and_1_out, neg);
  and and_3 (and_3_out, not_5_out, or_1_out);
  and and_4 (and_4_out, not_3_out, and_3_out);
  and and_5 (and_5_out, s0, clr);
  and and_6 (and_6_out, s1, or_2_out);
  or or_2 (or_2_out, clr, and_4_out);
  and and_7 (and_7_out, not_2_out, not_3_out);
  or or_3 (or_3_out, and_5_out, and_6_out);
  and and_8 (and_8_out, s2, not_2_out);
  and and_9 (and_9_out, and_7_out, pwr);
  and and_10 (and_10_out, not_4_out, or_3_out);
  and and_11 (and_11_out, and_8_out, not_4_out);
  or or_4 (or_4_out, and_9_out, and_10_out);
  and and_12 (and_12_out, and_11_out, clr);
  and and_13 (and_13_out, not_1_out, or_4_out);
  or or_5 (n0_clr, and_12_out, and_13_out);
endmodule

module number_decoder (
  input  [3:0] in_1,
  output num_0,
  output num_1,
  output num_2,
  output num_3,
  output num_4,
  output num_5,
  output num_6,
  output num_7,
  output num_8,
  output num_9
);

  wire and_1_out, and_2_out, and_3_out, and_4_out, and_5_out, and_6_out, and_7_out, and_8_out, and_9_out,
       and_10_out, and_11_out, and_12_out, and_13_out, and_14_out, and_15_out, and_16_out, and_17_out,
       and_18_out, and_19_out, and_20_out, not_1_out, not_2_out, not_3_out, not_4_out;

  not not_1 (not_1_out, in_1[0]);
  not not_2 (not_2_out, in_1[1]);
  not not_3 (not_3_out, in_1[2]);
  not not_4 (not_4_out, in_1[3]);
  and and_1 (and_1_out, not_1_out, not_2_out);
  and and_2 (and_2_out, in_1[0], not_2_out);
  and and_3 (and_3_out, not_1_out, in_1[1]);
  and and_4 (and_4_out, in_1[0], in_1[1]);
  and and_5 (and_5_out, not_1_out, not_2_out);
  and and_6 (and_6_out, in_1[0], not_2_out);
  and and_7 (and_7_out, not_1_out, in_1[1]);
  and and_8 (and_8_out, in_1[0], in_1[1]);
  and and_9 (and_9_out, not_1_out, not_2_out);
  and and_10 (and_10_out, in_1[0], not_2_out);
  and and_11 (and_11_out, and_1_out, not_3_out);
  and and_12 (and_12_out, and_2_out, not_3_out);
  and and_13 (and_13_out, and_3_out, not_3_out);
  and and_14 (and_14_out, and_4_out, not_3_out);
  and and_15 (and_15_out, and_5_out, in_1[2]);
  and and_16 (and_16_out, and_6_out, in_1[2]);
  and and_17 (and_17_out, and_7_out, in_1[2]);
  and and_18 (and_18_out, and_8_out, in_1[2]);
  and and_19 (and_19_out, and_9_out, not_3_out);
  and and_20 (and_20_out, and_10_out, not_3_out);
  and and_21 (num_0, and_11_out, not_4_out);
  and and_22 (num_1, and_12_out, not_4_out);
  and and_23 (num_2, and_13_out, not_4_out);
  and and_24 (num_3, and_14_out, not_4_out);
  and and_25 (num_4, and_15_out, not_4_out);
  and and_26 (num_5, and_16_out, not_4_out);
  and and_27 (num_6, and_17_out, not_4_out);
  and and_28 (num_7, and_18_out, not_4_out);
  and and_29 (num_8, and_19_out, in_1[3]);
  and and_30 (num_9, and_20_out, in_1[3]);
endmodule

module num_encoder (
  input  n0,
  input  n1,
  input  n2,
  input  n3,
  input  n4,
  input  n5,
  input  n6,
  input  n7,
  input  n8,
  input  n9,
  output [3:0] out_11
);

  wire and_1_out, and_2_out, and_3_out, and_4_out, and_5_out, and_6_out, and_7_out, and_8_out, and_9_out,
       and_10_out, and_12_out, and_13_out, and_14_out, and_15_out, and_16_out, and_17_out, and_18_out,
       and_19_out, and_20_out, not_3_out, not_4_out, not_5_out, not_6_out, not_7_out, not_8_out, not_9_out,
       not_10_out, or_1_out, or_2_out, or_4_out, or_5_out, or_6_out, or_7_out, or_8_out, or_10_out;

  and and_1 (and_1_out, n1, not_3_out);
  // NOT_Gate not_1 has open pins: in=n0, out=open
  and and_2 (and_2_out, and_1_out, not_4_out);
  or or_1 (or_1_out, and_2_out, n3);
  and and_3 (and_3_out, not_8_out, not_9_out);
  and and_4 (and_4_out, not_7_out, and_3_out);
  and and_5 (and_5_out, not_6_out, and_4_out);
  and and_6 (and_6_out, not_5_out, and_5_out);
  and and_7 (and_7_out, or_1_out, and_6_out);
  or or_2 (or_2_out, and_7_out, and_10_out);
  or or_3 (out_11[0], or_2_out, n9);
  // NOT_Gate not_2 has open pins: in=n1, out=open
  and and_8 (and_8_out, n5, not_7_out);
  and and_9 (and_9_out, and_8_out, not_8_out);
  or or_4 (or_4_out, and_9_out, n7);
  and and_10 (and_10_out, or_4_out, not_9_out);
  not not_3 (not_3_out, n2);
  xor xor_1 (out_11[3], n8, n9);
  not not_4 (not_4_out, n3);
  or or_5 (or_5_out, n4, n5);
  not not_5 (not_5_out, n4);
  or or_6 (or_6_out, or_5_out, n6);
  or or_7 (or_7_out, or_6_out, n7);
  and and_11 (out_11[2], or_7_out, and_12_out);
  not not_6 (not_6_out, n5);
  and and_12 (and_12_out, not_10_out, not_9_out);
  not not_7 (not_7_out, n6);
  and and_13 (and_13_out, not_7_out, and_19_out);
  and and_14 (and_14_out, not_6_out, and_13_out);
  or or_8 (or_8_out, n2, n3);
  and and_15 (and_15_out, not_5_out, and_14_out);
  and and_16 (and_16_out, or_8_out, and_15_out);
  and and_17 (and_17_out, or_10_out, and_20_out);
  or or_9 (out_11[1], and_16_out, and_17_out);
  not not_8 (not_8_out, n7);
  and and_18 (and_18_out, not_9_out, not_10_out);
  and and_19 (and_19_out, not_8_out, and_18_out);
  or or_10 (or_10_out, n6, n7);
  not not_9 (not_9_out, n8);
  and and_20 (and_20_out, not_9_out, not_9_out);
  not not_10 (not_10_out, n9);
endmodule

module op_encoder (
  input  add,
  input  sub,
  input  div,
  input  mult,
  output [2:0] out_5
);

  wire and_1_out, and_2_out, not_1_out, not_2_out, not_3_out, or_1_out, or_2_out;

  not not_1 (not_1_out, sub);
  not not_2 (not_2_out, div);
  not not_3 (not_3_out, mult);
  and and_1 (and_1_out, not_1_out, not_2_out);
  or or_1 (or_1_out, sub, div);
  and and_2 (and_2_out, add, and_1_out);
  and and_3 (out_5[1], or_1_out, not_3_out);
  or or_2 (or_2_out, and_2_out, div);
  and and_4 (out_5[0], or_2_out, not_3_out);

  assign out_5[2] = mult;
endmodule

module op_decoder (
  input  b0,
  input  b1,
  input  b2,
  output add,
  output sub,
  output div,
  output mult
);

  wire and_1_out, and_2_out, and_3_out, and_4_out, not_1_out, not_2_out, not_3_out;

  not not_1 (not_1_out, b1);
  not not_2 (not_2_out, b2);
  not not_3 (not_3_out, b0);
  and and_1 (and_1_out, b0, not_1_out);
  and and_2 (and_2_out, b1, not_2_out);
  and and_3 (and_3_out, b1, not_2_out);
  and and_4 (and_4_out, b2, not_1_out);
  and and_5 (add, and_1_out, not_2_out);
  and and_6 (sub, and_2_out, not_3_out);
  and and_7 (div, and_3_out, b0);
  and and_8 (mult, and_4_out, not_3_out);
endmodule

module datapath (
  input  val1_en,
  input  clr,
  input  enables,
  input  n_or_i,
  input  [3:0] num_val,
  input  [2:0] op_code
);

  wire clock_1_out, clock_2_out, clock_3_out;
  wire [2:0] and_3_out, bit_extender_3_out, not_4_out;
  wire [31:0] adder_1_out, adder_2_out, adder_3_out, and_1_out, and_2_out, bit_extender_1_out,
       bit_extender_2_out, divider_1_out, multiplexer_1_out, multiplexer_2_out, multiplexer_3_out,
       multiplier_1_out, multiplier_2_out, not_1_out, not_2_out, not_3_out, value1_q;

  assign bit_extender_1_out = {{31{clr}}, clr};  // Bit_Extender bit_extender_1
  assign not_1_out = ~value1_q;  // NOT_Gate not_1, 32 bits wide
  assign not_2_out = ~bit_extender_1_out;  // NOT_Gate not_2, 32 bits wide
  Adder #(.width(32)) adder_1 (.a(not_1_out), .b({32{1'b0}}), .out(adder_1_out), .cin(n_or_i));  // open: cout
  Multiplier #(.width(32)) multiplier_1 (.a(32'ha), .b(value1_q), .out(multiplier_1_out));  // open: cin, cout
  assign bit_extender_2_out = {{28{num_val[3]}}, num_val};  // Bit_Extender bit_extender_2
  assign bit_extender_3_out = {{2{clr}}, clr};  // Bit_Extender bit_extender_3
  Adder #(.width(32)) adder_2 (.a(multiplier_1_out), .b(bit_extender_2_out), .out(adder_2_out));  // open: cin, cout
  assign and_1_out = not_2_out & multiplexer_1_out;  // AND_Gate and_1, 32 bits wide
  Multiplexer #(.width(32)) multiplexer_1 (.in0(adder_1_out), .in1(adder_2_out), .out(multiplexer_1_out), .sel(n_or_i));
  assign not_3_out = ~value1_q;  // NOT_Gate not_3, 32 bits wide
  assign not_4_out = ~bit_extender_3_out;  // NOT_Gate not_4, 3 bits wide
  Register #(.width(32)) value1 (.D(and_1_out), .en(val1_en), .clk(clock_1_out), .Q(value1_q));  // open: clr
  Clock clock_1 (.out(clock_1_out));
  Multiplexer #(.width(32)) multiplexer_2 (.in0(value1_q), .in1(not_3_out), .out(multiplexer_2_out), .sel(op_code[2]));
  Adder #(.width(32)) adder_3 (
    .a(multiplexer_3_out), .b(multiplexer_2_out), .out(adder_3_out), .cin(op_code[2]));  // open: cout
  Divider #(.width(32)) divider_1 (.a(value1_q), .b(multiplexer_3_out), .out(divider_1_out));  // open: upper, rem
  Multiplier #(.width(32)) multiplier_2 (
    .a(multiplexer_3_out), .b(value1_q), .out(multiplier_2_out));  // open: cin, cout
  Clock clock_2 (.out(clock_2_out));
  assign and_2_out = not_2_out & multiplexer_3_out;  // AND_Gate and_2, 32 bits wide
  Register #(.width(32)) value2 (.D(and_2_out), .en(enables), .clk(clock_2_out), .Q(adder_3_out));  // open: clr
  Multiplexer #(.select(3), .width(32)) multiplexer_3 (
    .in0(adder_3_out), .in1(adder_3_out), .in2(adder_3_out), .in3(divider_1_out), .in4(multiplier_2_out),
    .out(multiplexer_3_out), .sel(op_code));  // open: in5, in6, in7
  assign and_3_out = not_4_out & op_code;  // AND_Gate and_3, 3 bits wide
  Register #(.width(3)) register_1 (.D(and_3_out), .en(enables), .clk(clock_3_out), .Q(op_code));  // open: clr
  Clock clock_3 (.out(clock_3_out));

  // Notes on the sheet:
  //   sub_ctr
endmodule

module clear_reg (
  input  clr,
  output [31:0] out_2
);
endmodule
